# Fritzing sketch shast-fritzing (saved by Fritzing 0.9.2b)
breadboards: 1

parts:
  Part1 = Soil Moisture Sensor
  Part2 = Arduino Yun
  R1 = Photocell (LDR) [package=THT]
  RHT1 = Humidity and Temperature Sensor RHT03
  R2 = Resistor [tolerance=±5% resistance=220 package=THT]

nets:
  N1: Part1.SIG, Part2.A2
  GND: Part1.GND, Part2.GND, RHT1.GND_2, R2.Pin_1
  VCC: Part1.VCC, Part2.5V, R1.pin_0, RHT1.Vcc
  N2: Part2.A1, R1.pin_1, R2.Pin_0
  N3: Part2.D7, RHT1.Data-signal
